# Fritzing sketch BeeHive (saved by Fritzing 1.0.6)
stripboards: 2

parts:
  A3 = ina226 module
  A4 = ina226 module
  U1 = LIPO-2000mAh [package=lipo-2000]
  A5 = CN3065 Mini Solar Charger Module
  VR1 = HT7833 LDO [package="TO92 [THT]"]
  C1 = Electrolytic Capacitor [capacitance=1mF voltage=10V package="100 mil [THT, electrolytic]"]
  D1 = SOLAR-IXYS [package=solarbit-12x1]
  Adafruit_NAU7802_Breakout_Rev_C1 = Adafruit NAU7802 Breakout Rev C [mn=Adafruit mpn=#4538 part_number=#4538]
  A6 = featherS3
  Part1 = INMP441
  U2 = SHT40 Breakout [mn=Sensirion package="Breakout Module [THT]"]

nets (from the schematic view):
  N1: A3.Pin_1, U1.+
  N2: A3.Pin_2, A3.Pin_3, A5.Pin_7, A5.Pin_9, VR1.Vin
  N3: A3.Pin_5, A4.Pin_5, Adafruit_NAU7802_Breakout_Rev_C1.SCL, A6.Pin_22, U2.SCL
  N4: A3.Pin_6, A4.Pin_6, Adafruit_NAU7802_Breakout_Rev_C1.SDA, A6.Pin_21, U2.SDA
  GND: A3.Pin_7, A4.Pin_2, A4.Pin_3, A4.Pin_7, A4.Pin_12, U1.-, A5.Pin_2, A5.Pin_8, A5.Pin_10, VR1.GND, C1.-, Adafruit_NAU7802_Breakout_Rev_C1.GND, A6.Pin_4, A6.Pin_17, A6.Pin_33, A6.Pin_38, Part1.GND, U2.GND
  VCC: A3.Pin_8, A3.Pin_10, A4.Pin_8, A4.Pin_10, Adafruit_NAU7802_Breakout_Rev_C1.VCC, A6.Pin_16, Part1.VDD, U2.VIN
  N5: A4.Pin_1, D1.C
  N6: A5.Pin_1, D1.A
  N7: VR1.Vout, C1.+, A6.Pin_2
  N8: A6.Pin_9, Part1.WS
  N9: A6.Pin_10, Part1.SD
  N10: A6.Pin_11, Part1.SCK

custom parts:
  ina226 module: INA226 Voltage Current/Power Monitoring Sensor Module IIC I2C Interface Bi-directional INA226 Module CJMCU-226.
  CN3065 Mini Solar Charger Module: Fc-51 Infrared Obstacle Avoidance Proximity Sensor module. IR transmitter led, receiver LED, lm393 compaitor and a pot. 3.3 V to 5V power.
  HT7833 LDO: An HT7833 Low Dropout Fixed Voltage Regulator.
  featherS3: FeatherS3 is the latest in our super popular ESP32 based Feather boards.
  INMP441: This is a simple breakout board for the INMP441 I2S MEMS microphone.
  SHT40 Breakout: SHT40 Temperature and Humidity Sensor Breakout Module. Sensirion SHT40 with I2C interface (address 0x44). 10mm x 13mm purple PCB with 4-pin header (VIN, GND, SCL, SDA).
